# Fritzing sketch Termostat (saved by Fritzing 0.9.3b)
breadboards: 1

parts:
  RHT1 = Humidity and Temperature Sensor RHT03
  Grove1 = Grove 4 Digit Display
  U2 = 2-Channel 5v Relay Shield [package=relay-2ch5v10a]
  IC1 = DIP - 4 pins [chip_label=IC package="DIP (Dual Inline) [THT]"]  # not connected
  U4 = ESP8266 WiFi Module [part_number=ESP8266]
  S1 = Pushbutton [package="[THT]"]
  Power_plug1 = Power plug

nets:
  VCC: RHT1.Vcc, Grove1.VCC, U2.VCC, U4.VCC, Power_plug1.VCC
  N1: RHT1.Data-signal, U4.GPIO_2
  GND: RHT1.GND_2, Grove1.GND, U2.GND, U4.GPIO_0, U4.GND, S1.Pin_3, S1.Pin_4, Power_plug1.GND
  N2: Grove1.DIO, U4.GPIO_4
  N3: Grove1.CLK, U4.GPIO_5
  N4: U2.IN1, U4.GPIO_12
  N5: U2.IN2, U4.GPIO_14

notes:
  Зажать при прошивке

custom parts:
  2-Channel 5v Relay Shield: 2 Channel 5v Relay Shield w. 2x SPD-06VDC-SD-C
  DIP - 4 pins: A DIP stand-in part for whatever IC you want. With 4 pins on a 300mil dual inline package (DIP) footprint.
  ESP8266 WiFi Module: Generic WiFi Module based on the ESP8266 with onboard PCB antenna and UART communications
